// Logisim project Rodberg_Final_Kitchen_Sink_V2_WORKING.circ as structural Verilog
module _16_bit_ALU (
  input  [15:0] A,
  input  [15:0] B,
  input  [1:0] ALU_Op,
  output [15:0] ALU_Out
);

  wire and_1_out;
  wire [15:0] adder_1_out, and_2_out, multiplexer_1_out, not_1_out, or_1_out;

  Multiplexer #(.width(16), .enable("false")) multiplexer_1 (
    .in0(B), .in1(not_1_out), .out(multiplexer_1_out), .sel(and_1_out));
  assign not_1_out = ~B;  // NOT_Gate not_1, 16 bits wide
  and and_1 (and_1_out, ALU_Op[0], ALU_Op[1]);
  Adder #(.width(16)) adder_1 (.a(A), .b(multiplexer_1_out), .out(adder_1_out), .cin(and_1_out));  // open: cout
  assign and_2_out = multiplexer_1_out & A;  // AND_Gate and_2, 16 bits wide
  assign or_1_out = multiplexer_1_out | A;  // OR_Gate or_1, 16 bits wide
  Multiplexer #(.select(2), .width(16), .enable("false")) multiplexer_2 (
    .in0(adder_1_out), .in1(and_2_out), .in2(or_1_out), .in3(adder_1_out), .out(ALU_Out), .sel(ALU_Op));

  // Notes on the sheet:
  //   4 Bit ALU
  //   00 = ADD
  //   01 = AND
  //   10 = OR
  //   11 = SUB
  //   sub not B
  //   sub cin
  //   sub
endmodule

module _8x16_bit_Register_File (
  input  [15:0] Data_In,
  input  [2:0] Read_Addr_1,
  input  Write_Enable,
  input  [2:0] Write_Addr,
  input  [2:0] Read_Addr_2,
  input  Clock,
  output [15:0] Read_1_Data,
  output [15:0] Read_2_Data
);

  wire demultiplexer_1_out0, demultiplexer_1_out1, demultiplexer_1_out2, demultiplexer_1_out3,
       demultiplexer_1_out4, demultiplexer_1_out5, demultiplexer_1_out6, demultiplexer_1_out7;
  wire [15:0] register_1_q, register_2_q, register_3_q, register_4_q, register_5_q, register_6_q,
       register_7_q, register_8_q;

  Demultiplexer #(.select(3), .enable("false")) demultiplexer_1 (
    .out0(demultiplexer_1_out0), .out1(demultiplexer_1_out1), .out2(demultiplexer_1_out2),
    .out3(demultiplexer_1_out3), .out4(demultiplexer_1_out4), .out5(demultiplexer_1_out5),
    .out6(demultiplexer_1_out6), .out7(demultiplexer_1_out7), .in(Write_Enable), .sel(Write_Addr));
  Register #(.width(16)) register_1 (
    .D(Data_In), .en(demultiplexer_1_out0), .Q(register_1_q), .clk(Clock));  // open: clr
  Register #(.width(16)) register_2 (
    .D(Data_In), .en(demultiplexer_1_out1), .Q(register_2_q), .clk(Clock));  // open: clr
  Register #(.width(16)) register_3 (
    .D(Data_In), .en(demultiplexer_1_out2), .Q(register_3_q), .clk(Clock));  // open: clr
  Register #(.width(16)) register_4 (
    .D(Data_In), .en(demultiplexer_1_out3), .Q(register_4_q), .clk(Clock));  // open: clr
  Register #(.width(16)) register_5 (
    .D(Data_In), .en(demultiplexer_1_out4), .Q(register_5_q), .clk(Clock));  // open: clr
  Register #(.width(16)) register_6 (
    .D(Data_In), .en(demultiplexer_1_out5), .Q(register_6_q), .clk(Clock));  // open: clr
  Register #(.width(16)) register_7 (
    .D(Data_In), .en(demultiplexer_1_out6), .Q(register_7_q), .clk(Clock));  // open: clr
  Register #(.width(16)) register_8 (
    .D(Data_In), .en(demultiplexer_1_out7), .Q(register_8_q), .clk(Clock));  // open: clr
  Multiplexer #(.select(3), .width(16), .enable("false")) multiplexer_1 (
    .in0(register_1_q), .in1(register_2_q), .in2(register_3_q), .in3(register_4_q), .in4(register_5_q),
    .in5(register_6_q), .in6(register_7_q), .in7(register_8_q), .out(Read_1_Data), .sel(Read_Addr_1));
  Multiplexer #(.select(3), .width(16), .enable("false")) multiplexer_2 (
    .in0(register_1_q), .in1(register_2_q), .in2(register_3_q), .in3(register_4_q), .in4(register_5_q),
    .in5(register_6_q), .in6(register_7_q), .in7(register_8_q), .out(Read_2_Data), .sel(Read_Addr_2));

  // Notes on the sheet:
  //   8x4-bit Register File
endmodule

module ALU_REG_Instruction (
  input  [13:0] in_1,
  input  clock,
  output [3:0] CPU_Op_Out
);

  wire n8x16_bit_register_file_1_p7;
  wire [3:0] bit_extender_1_out, multiplexer_1_out, n8x16_bit_register_file_1_p8;

  // Probe on nothing
  // _8x16_bit_Register_File 8x16_bit_register_file_1: pin names not known; wires that end beside it: CPU_Op_Out, 1'b1, clock, in_1[8:6], in_1[5:3], in_1[2:0], n8x16_bit_register_file_1_p7, n8x16_bit_register_file_1_p8
  Multiplexer #(.width(4), .enable("false")) multiplexer_1 (
    .in0(n8x16_bit_register_file_1_p8), .in1(bit_extender_1_out), .out(multiplexer_1_out), .sel(in_1[13]));
  assign bit_extender_1_out = {{1{in_1[2]}}, in_1[2:0]};  // Bit_Extender bit_extender_1
  // _16_bit_ALU 16_bit_alu_1: pin names not known; wires that end beside it: n8x16_bit_register_file_1_p7, multiplexer_1_out, in_1[10:9], CPU_Op_Out

  // Notes on the sheet:
  //   op
  //   src2
  //   src1
  //   immed data
  //   immed select
  //   ALU op
  //   dest
endmodule

module ALU_With_Mem (
  input  [13:0] in_1,
  input  clock,
  output [3:0] CPU_Op_Out
);

  wire control_logic_1_p2, control_logic_1_p3, control_logic_1_p4, control_logic_1_p5, control_logic_1_p6,
       n8x16_bit_register_file_1_p7;
  wire [2:0] multiplexer_1_out;
  wire [3:0] bit_extender_1_out, multiplexer_2_out, multiplexer_3_out, n8x16_bit_register_file_1_p8,
       ram_1_data;

  // Probe on nothing
  // Control_Logic control_logic_1: pin names not known; wires that end beside it: in_1[13:9], control_logic_1_p2, control_logic_1_p3, control_logic_1_p4, control_logic_1_p5, control_logic_1_p6
  Multiplexer #(.width(3), .enable("false")) multiplexer_1 (
    .in0(in_1[2:0]), .in1(in_1[8:6]), .out(multiplexer_1_out), .sel(control_logic_1_p4));
  Multiplexer #(.width(4), .enable("false")) multiplexer_2 (
    .in0(CPU_Op_Out), .in1(ram_1_data), .out(multiplexer_2_out), .sel(control_logic_1_p3));
  // _8x16_bit_Register_File 8x16_bit_register_file_1: pin names not known; wires that end beside it: multiplexer_2_out, control_logic_1_p5, clock, in_1[8:6], in_1[5:3], multiplexer_1_out, n8x16_bit_register_file_1_p7, n8x16_bit_register_file_1_p8
  Multiplexer #(.width(4), .enable("false")) multiplexer_3 (
    .in0(n8x16_bit_register_file_1_p8), .in1(bit_extender_1_out), .out(multiplexer_3_out),
    .sel(control_logic_1_p2));
  assign bit_extender_1_out = {{1{in_1[2]}}, in_1[2:0]};  // Bit_Extender bit_extender_1
  // _16_bit_ALU 16_bit_alu_1: pin names not known; wires that end beside it: n8x16_bit_register_file_1_p7, multiplexer_3_out, control_logic_1_p6, CPU_Op_Out
  RAM #(.addrWidth(4), .dataWidth(4), .bus("separate")) ram_1 (
    .addr(CPU_Op_Out), .din(n8x16_bit_register_file_1_p8), .data(ram_1_data), .sel(1'b1), .clk(clock),
    .ld(control_logic_1_p3));  // open: str, clr

  // Notes on the sheet:
  //   op
  //   src2
  //   src1
  //   immed data
  //   immed select
  //   ALU op
  //   dest
endmodule

module Control_Logic (
  input  [4:0] in_1,
  output IMMED_Select,
  output sw_bit,
  output lw_bit,
  output [1:0] ALU_OP
);


  assign ALU_OP = {in_1[0], in_1[1]};
  assign IMMED_Select = in_1[4];
  assign lw_bit = in_1[2];
  assign sw_bit = in_1[3];
endmodule

module Full_CPU (
  input  clock
);

  wire control_logic_1_immed_select, control_logic_1_lw_bit, control_logic_1_sw_bit;
  wire [1:0] control_logic_1_alu_op;
  wire [2:0] multiplexer_1_out;
  wire [7:0] adder_1_out, register_1_q;
  wire [13:0] ram_1_data;
  wire [15:0] bit_extender_1_out, multiplexer_2_out, multiplexer_3_out,
       n8x16_bit_register_file_1_read_1_data, n8x16_bit_register_file_1_read_2_data, n16_bit_alu_1_alu_out,
       ram_2_data;

  Adder adder_1 (.a(register_1_q), .b(8'h1), .out(adder_1_out));  // open: cin, cout
  Register register_1 (.D(adder_1_out), .Q(register_1_q), .clk(clock));  // open: en, clr
  RAM #(.dataWidth(14)) ram_1 (.addr(register_1_q), .data(ram_1_data));  // open: sel, clk, ld, clr
  Multiplexer #(.width(3), .enable("false")) multiplexer_1 (
    .in0(ram_1_data[2:0]), .in1(ram_1_data[5:3]), .out(multiplexer_1_out), .sel(control_logic_1_sw_bit));
  Control_Logic control_logic_1 (
    .in_1(ram_1_data[13:9]), .IMMED_Select(control_logic_1_immed_select), .sw_bit(control_logic_1_sw_bit),
    .lw_bit(control_logic_1_lw_bit), .ALU_OP(control_logic_1_alu_op));
  Multiplexer #(.width(16), .enable("false")) multiplexer_2 (
    .in0(n16_bit_alu_1_alu_out), .in1(ram_2_data), .out(multiplexer_2_out), .sel(control_logic_1_lw_bit));
  _8x16_bit_Register_File u_8x16_bit_register_file_1 (
    .Data_In(multiplexer_2_out), .Write_Enable(1'b1), .Clock(clock), .Write_Addr(ram_1_data[8:6]),
    .Read_Addr_1(ram_1_data[5:3]), .Read_Addr_2(multiplexer_1_out),
    .Read_1_Data(n8x16_bit_register_file_1_read_1_data), .Read_2_Data(n8x16_bit_register_file_1_read_2_data));
  assign bit_extender_1_out = {{13{ram_1_data[2]}}, ram_1_data[2:0]};  // Bit_Extender bit_extender_1
  Multiplexer #(.width(16), .enable("false")) multiplexer_3 (
    .in0(n8x16_bit_register_file_1_read_2_data), .in1(bit_extender_1_out), .out(multiplexer_3_out),
    .sel(control_logic_1_immed_select));
  _16_bit_ALU u_16_bit_alu_1 (
    .A(n8x16_bit_register_file_1_read_1_data), .B(multiplexer_3_out), .ALU_Op(control_logic_1_alu_op),
    .ALU_Out(n16_bit_alu_1_alu_out));
  RAM #(.addrWidth(16), .dataWidth(16), .bus("separate")) ram_2 (
    .addr(n16_bit_alu_1_alu_out), .din(n8x16_bit_register_file_1_read_2_data), .data(ram_2_data),
    .str(control_logic_1_sw_bit), .sel(1'b1), .clk(clock), .ld(control_logic_1_lw_bit));  // open: clr

  // Notes on the sheet:
  //   Sam
  //   op
  //   src2
  //   ALU op
  //   dest
  //   src1
  //   immed data
  //   immed select
endmodule
